// Logisim project ARM_Control_Unit_Multicycle.circ as structural Verilog
module ARM_Control_Unit_Multicycle (
  input  Clk,
  input  [3:0] Cond,
  input  [3:0] ALUFlags,
  input  [3:0] Rd,
  input  [1:0] Op,
  input  [5:0] Funct,
  output PCWrite,
  output RegWrite,
  output MemWrite,
  output IRWrite,
  output AdrSrc,
  output [1:0] ResultSrc,
  output ALUSrcA,
  output [1:0] ALUSrcB,
  output [1:0] ALUControl,
  output [1:0] ImmSrc,
  output [1:0] RegSrc
);

  wire arm_decoder_1_memw, arm_decoder_1_nextpc, arm_decoder_1_pcs, arm_decoder_1_regw;
  wire [1:0] arm_decoder_1_flagw;

  ARM_Decoder arm_decoder_1 (
    .Rd(Rd), .Clk(Clk), .Op(Op), .Funct(Funct), .PCS(arm_decoder_1_pcs), .RegW(arm_decoder_1_regw),
    .MemW(arm_decoder_1_memw), .IRWrite(IRWrite), .NextPC(arm_decoder_1_nextpc), .AdrSrc(AdrSrc),
    .ResultSrc(ResultSrc), .ALUSrcA(ALUSrcA), .ALUSrcB(ALUSrcB), .ALUControl(ALUControl),
    .FlagW(arm_decoder_1_flagw), .ImmSrc(ImmSrc), .RegSrc(RegSrc));
  ARM_Conditional_Logic arm_conditional_logic_1 (
    .ALUFlags(ALUFlags), .FlagW(arm_decoder_1_flagw), .Clk(Clk), .Cond(Cond), .MemW(arm_decoder_1_memw),
    .RegW(arm_decoder_1_regw), .PCS(arm_decoder_1_pcs), .NextPC(arm_decoder_1_nextpc), .PCWrite(PCWrite),
    .RegWrite(RegWrite), .MemWrite(MemWrite));

  // Notes on the sheet:
  //   The layout is a bit of a rat's nest, but ultimately the I/O pin order was the goal to make the higher level organization easier
endmodule

module ARM_PC_logic (
  input  [3:0] Rd,
  input  RegW,
  input  Branch,
  output PCS
);

  wire and_1_out, equality_4_bit_1_eq;

  Equality_4_bit equality_4_bit_1 (.A(4'b1111), .B(Rd), .EQ(equality_4_bit_1_eq));
  and and_1 (and_1_out, equality_4_bit_1_eq, RegW);
  or or_1 (PCS, and_1_out, Branch);

  // Notes on the sheet:
  //   PCS = ((Rd ==15) & RegW) | Branch
endmodule

module ARM_ALU_Decoder (
  input  ALUOp,
  input  [3:0] cmd,
  input  S,
  output [1:0] ALUControl,
  output [1:0] FlagW
);

  wire and_1_out, and_2_out, and_3_out, or_1_out, or_2_out, or_3_out;

  and and_1 (and_1_out, ~cmd[1], ~cmd[2]);  // AND_Gate
  and and_2 (and_2_out, ~cmd[1], cmd[3]);  // AND_Gate
  or or_1 (or_1_out, cmd[1], cmd[3]);
  or or_2 (or_2_out, and_1_out, and_2_out);
  and and_3 (and_3_out, cmd[2], ~cmd[3]);  // AND_Gate
  and and_4 (ALUControl[0], ALUOp, or_1_out);
  and and_5 (ALUControl[1], ALUOp, or_2_out);
  or or_3 (or_3_out, cmd[1], and_3_out);
  and and_6 (FlagW[1], ALUOp, S);
  and and_7 (FlagW[0], or_3_out, FlagW[1]);
endmodule

module Equality_4_bit (
  input  [3:0] A,
  input  [3:0] B,
  output EQ
);

  wire xnor_1_out, xnor_2_out, xnor_3_out, xnor_4_out;

  xnor xnor_1 (xnor_1_out, A[0], B[0]);
  xnor xnor_2 (xnor_2_out, A[1], B[1]);
  xnor xnor_3 (xnor_3_out, A[2], B[2]);
  xnor xnor_4 (xnor_4_out, A[3], B[3]);
  and and_1 (EQ, xnor_1_out, xnor_2_out, xnor_3_out, xnor_4_out);
endmodule

module ARM_Decoder (
  input  [3:0] Rd,
  input  Clk,
  input  [1:0] Op,
  input  [5:0] Funct,
  output PCS,
  output RegW,
  output MemW,
  output IRWrite,
  output NextPC,
  output AdrSrc,
  output [1:0] ResultSrc,
  output ALUSrcA,
  output [1:0] ALUSrcB,
  output [1:0] ALUControl,
  output [1:0] FlagW,
  output [1:0] ImmSrc,
  output [1:0] RegSrc
);

  wire arm_main_fsm_1_aluop, arm_main_fsm_1_branch;

  ARM_Main_FSM arm_main_fsm_1 (
    .Clk(Clk), .Op(Op), .Funct5(Funct[5]), .Funct0(Funct[0]), .Branch(arm_main_fsm_1_branch), .RegW(RegW),
    .MemW(MemW), .IRWrite(IRWrite), .NextPC(NextPC), .AdrSrc(AdrSrc), .ResultSrc(ResultSrc),
    .ALUSrcA(ALUSrcA), .ALUSrcB(ALUSrcB), .ALUOp(arm_main_fsm_1_aluop));
  ARM_ALU_Decoder arm_alu_decoder_1 (
    .ALUOp(arm_main_fsm_1_aluop), .cmd(Funct[4:1]), .S(Funct[0]), .ALUControl(ALUControl), .FlagW(FlagW));
  ARM_Instr_Decoder arm_instr_decoder_1 (.Op(Op), .ImmSrc(ImmSrc), .RegSrc(RegSrc));
  ARM_PC_logic arm_pc_logic_1 (.Rd(Rd), .RegW(RegW), .Branch(arm_main_fsm_1_branch), .PCS(PCS));
endmodule

module ARM_Condition_Check (
  input  [3:0] Cond,
  input  [3:0] ALUFlags,
  output CondEx
);

  wire and_1_out, and_2_out, not_1_out, not_2_out, not_3_out, not_4_out, not_5_out, not_6_out, not_7_out,
       xor_1_out;

  xor xor_1 (xor_1_out, ALUFlags[3], ALUFlags[0]);
  and and_1 (and_1_out, ~ALUFlags[2], ALUFlags[1]);  // AND_Gate
  not not_1 (not_1_out, xor_1_out);
  and and_2 (and_2_out, not_1_out, ~ALUFlags[2]);  // AND_Gate
  not not_2 (not_2_out, ALUFlags[2]);
  not not_3 (not_3_out, ALUFlags[1]);
  not not_4 (not_4_out, ALUFlags[3]);
  not not_5 (not_5_out, ALUFlags[0]);
  not not_6 (not_6_out, and_1_out);
  not not_7 (not_7_out, and_2_out);
  Multiplexer #(.select(4)) multiplexer_1 (
    .in0(ALUFlags[2]), .in1(not_2_out), .in2(ALUFlags[1]), .in3(not_3_out), .in4(ALUFlags[3]),
    .in5(not_4_out), .in6(ALUFlags[0]), .in7(not_5_out), .in8(and_1_out), .in9(not_6_out), .in10(not_1_out),
    .in11(xor_1_out), .in12(and_2_out), .in13(not_7_out), .in14(1'b1), .out(CondEx), .sel(Cond));  // open: in15

  // Other names for the same wires on the sheet: V = ALUFlags[0]; C = ALUFlags[1]; Z = ALUFlags[2]; N = ALUFlags[3]

  // Notes on the sheet:
  //   Negative
  //   Zero
  //   Carry
  //   oVerflow
endmodule

module ARM_Conditional_Logic (
  input  [3:0] ALUFlags,
  input  [1:0] FlagW,
  input  Clk,
  input  [3:0] Cond,
  input  MemW,
  input  RegW,
  input  PCS,
  input  NextPC,
  output PCWrite,
  output RegWrite,
  output MemWrite
);

  wire and_1_out, and_2_out, and_3_out, arm_condition_check_1_condex, CondEx_q;
  wire [1:0] ALUFlags_01_q, ALUFlags_32_q;

  and and_1 (and_1_out, FlagW[1], arm_condition_check_1_condex);
  and and_2 (and_2_out, FlagW[0], arm_condition_check_1_condex);
  Register #(.width(2)) ALUFlags_32 (.D(ALUFlags[3:2]), .en(and_1_out), .clk(Clk), .Q(ALUFlags_32_q));  // open: clr
  Register #(.width(2)) ALUFlags_01 (.D(ALUFlags[1:0]), .en(and_2_out), .clk(Clk), .Q(ALUFlags_01_q));  // open: clr
  Register #(.width(1)) CondEx (.D(arm_condition_check_1_condex), .en(1'b1), .clk(Clk), .Q(CondEx_q));  // open: clr
  ARM_Condition_Check arm_condition_check_1 (
    .Cond(Cond), .ALUFlags({ALUFlags_32_q, ALUFlags_01_q}), .CondEx(arm_condition_check_1_condex));
  or or_1 (PCWrite, NextPC, and_3_out);
  and and_3 (and_3_out, PCS, CondEx_q);
  and and_4 (RegWrite, RegW, CondEx_q);
  and and_5 (MemWrite, MemW, CondEx_q);

  // Other names for the same wires on the sheet: ALUFlags01[1:0] = ALUFlags[1:0]; ALUFlags32[1:0] = ALUFlags[3:2]

  // Notes on the sheet:
  //   TODO: Verify this!
endmodule

module ARM_Main_FSM_Test (
  input  [1:0] Op,
  input  Funct5,
  input  Funct0,
  output Branch,
  output RegW,
  output MemW,
  output IRWrite,
  output NextPC,
  output AdrSrc,
  output [1:0] ResultSrc,
  output ALUSrcA,
  output [1:0] ALUSrcB,
  output ALUOp
);

  wire Clk_out;

  Clock Clk (.out(Clk_out));
  ARM_Main_FSM arm_main_fsm_1 (
    .Clk(Clk_out), .Op(Op), .Funct5(Funct5), .Funct0(Funct0), .Branch(Branch), .RegW(RegW), .MemW(MemW),
    .IRWrite(IRWrite), .NextPC(NextPC), .AdrSrc(AdrSrc), .ResultSrc(ResultSrc), .ALUSrcA(ALUSrcA),
    .ALUSrcB(ALUSrcB), .ALUOp(ALUOp));
endmodule

module ARM_Instr_Decoder (
  input  [1:0] Op,
  output [1:0] ImmSrc,
  output [1:0] RegSrc
);

  Equality_2_bit equality_2_bit_1 (.A(Op), .B(2'b01), .EQ(RegSrc[1]));
  Equality_2_bit equality_2_bit_2 (.A(Op), .B(2'b10), .EQ(RegSrc[0]));

  assign ImmSrc = Op;
endmodule

module Equality_2_bit (
  input  [1:0] A,
  input  [1:0] B,
  output EQ
);

  wire xnor_1_out, xnor_2_out;

  xnor xnor_1 (xnor_1_out, A[0], B[0]);
  xnor xnor_2 (xnor_2_out, A[1], B[1]);
  and and_1 (EQ, xnor_1_out, xnor_2_out);
endmodule

// VHDL entity ARM_Control_Unit_Testbench, as the project stores it:
--This self-checking test bench aims to verify the sequential aspects of the control unit. The combinational aspects are verified using a timing vector.
--In order to compensate for the timing issues associated with running VHDL simulations in Logisim-Evolution, the test signals are set on the rising edge
--of the clock and the test conditions are verified on the falling edge of the signal. This gives time for the external DUT to respond to the signals and
--allow its outputs (the testbench's inputs) to propagate back to the testbench. This approach was taken to be able to create a self-checking bench and 
--eliminate the need to manually inspect the timing diagrams.

--NOTE: Due to the complexity involved in determining the correct inputs for the sequential state, this effort was deemed more work than it was worth
--for now and the testbench is mainly used to coordinate the setting of various values and then the state and behavior of the circuit is inspected to
--ensure the state transitions occur when is necessary. Perhaps modify this to just do that? And have an input for the test scenario which is just a
--a configuration of signals... and then the user goes in and inspects the circuit to make sure it is correct? Might be easier?

library ieee; 
use ieee.std_logic_1164.all;
use ieee.numeric_std.all;

entity ARM_Control_Unit_Testbench is
	port(Clk		: in std_logic;
		Rst		: in std_logic;
		PCSrc	: in std_logic;
		MemToReg	: in std_logic;
		MemWrite	: in std_logic;
		ALUControl: in std_logic_vector(1 downto 0);
		ALUSrc	: in std_logic;
		ImmSrc	: in std_logic_vector(1 downto 0);
		RegWrite	: in std_logic;
		RegSrc	: in std_logic_vector(1 downto 0);
		Cond		: out std_logic_vector(3 downto 0);
		Op		: out std_logic_vector(1 downto 0);
		Funct	: out std_logic_vector(5 downto 0);
		Rd		: out std_logic_vector(3 downto 0);
		ALUFlags	: out std_logic_vector(3 downto 0)	--NZCV
		);
end;

architecture sim of ARM_Control_Unit_Testbench is
	function print_result(	pass : boolean;
						number: integer)
						return boolean is variable ret : boolean;
	begin
		if pass then
			report "Test " & integer'image(number) &" success.";
		else
			report "Test " & integer'image(number) &" failure.";
		end if;
		return ret;
	end function;
begin
	process(Clk) is
		variable ticks : integer := 0; 			--rising edge counter
		variable test_case_number : integer := 0;
		variable return_value : boolean := false; 	--value to store function return value as functions have to return values in VHDL
		constant testing_complete_message : String(1 to 16) := "Testing complete";
	begin
		if Rst = '1' then
			ticks := 0;
			test_case_number := 0;
		end if;

		--Set the control signals based on the corresponding test
		if rising_edge(Clk) then
			case test_case_number is
				when 0 =>
					report "Test case 0 entered";		
					Rd <= "0000"; 		--this value is irrelvant for these tests
					Op <= "00";		--the instruction needs to be data processing
					Funct <= "001001";	--cmd = ADD, the last bit is S to set conditional		
					Cond <= "0001";	--assign this to be NE as the registers are initialized to zeros
					ALUFlags <= "0100";	--ensure the Z flag is high
				when 1 =>
					
				when others =>
					report testing_complete_message;
			end case;
			ticks := ticks + 1;
		end if;
		
		--Verify the incoming signals (DUT output) are correct
		if falling_edge(Clk) then
			case test_case_number is
				when 0 =>
					--return_value := print_result(NOT_A = '1', test_case_number);
					test_case_number := test_case_number + 1;
				when 1 =>
					--return_value := print_result(NOT_B = '0', test_case_number);
					test_case_number := test_case_number + 1;
				when others =>
					report testing_complete_message;
			end case;
		end if;
	end process;
end architecture;

// VHDL entity ARM_Main_FSM, as the project stores it:
LIBRARY ieee;
USE ieee.std_logic_1164.all;

ENTITY ARM_Main_FSM IS
  PORT (
  ------------------------------------------------------------------------------
  --Input ports
    Clk		: IN std_logic;                    
    Op		: IN std_logic_vector(1 DOWNTO 0);
    Funct5	: IN std_logic;
    Funct0	: IN std_logic;
  ------------------------------------------------------------------------------
  --Output ports
    Branch	: OUT std_logic;
    RegW		: OUT std_logic;
    MemW		: OUT std_logic;
    IRWrite	: OUT std_logic;
    NextPC	: OUT std_logic;
    AdrSrc	: OUT std_logic;
    ResultSrc	: OUT std_logic_vector(1 DOWNTO 0);
    ALUSrcA	: OUT std_logic;
    ALUSrcB	: OUT std_logic_vector(1 DOWNTO 0);
    ALUOp		: OUT std_logic
    );
END ARM_Main_FSM;

ARCHITECTURE sim OF ARM_Main_FSM IS
	TYPE StateType IS (S0, S1, S2, S3, S4, S5, S6, S7, S8, S9);
	SIGNAL state     : StateType := S0;
	SIGNAL nextState : StateType := S1;

	FUNCTION state_to_string(s : stateType) RETURN STRING IS
	BEGIN
		CASE s is
			WHEN S0 =>
				RETURN "S0:Fetch";
			WHEN S1 =>
				RETURN "S1:Decode";
			WHEN S2 =>
				RETURN "S2:MemAdr";
			WHEN S3 =>
				RETURN "S3:MemRead";
			WHEN S4 =>
				RETURN "S4:MemWB";
			WHEN S5 =>
				RETURN "S5:MemWrite";
			WHEN S6 =>
				RETURN "S6:ExecuteR";
			WHEN S7 =>
				RETURN "S7:ExectuteI";
			WHEN S8 =>
				RETURN "S8:ALUWB";
			WHEN S9 =>
				RETURN "S9:Branch";
		END CASE;
	END FUNCTION;
BEGIN
	PROCESS(Clk) BEGIN
	--Synchronize state transitions with clock signal
		IF rising_edge(Clk) THEN
			report "Current state = " & state_to_string(state) & " -------> Next state = " & state_to_string(nextState);
			state <= nextState;
		END IF;

	--Output logic: For the sake of completeness all the output signals are listed. If a state doesn't care about a value it is set to 0.
	CASE state IS
		WHEN S0 =>
			Branch <= '0';
			RegW <= '0';
			MemW <= '0';
			IRWrite <= '1';
			NextPC <= '1';
			AdrSrc <= '0';
			ResultSrc <= "10";
			ALUSrcA <= '1';
			ALUSrcB <= "10";
			ALUOp <= '0';
		WHEN S1 =>
			Branch <= '0';
			RegW <= '0';
			MemW <= '0';
			IRWrite <= '0';
			NextPC <= '0';
			AdrSrc <= '0';
			ResultSrc <= "10";
			ALUSrcA <= '1';
			ALUSrcB <= "10";
			ALUOp <= '0';
		WHEN S2 =>
			Branch <= '0';
			RegW <= '0';
			MemW <= '0';
			IRWrite <= '0';
			NextPC <= '0';
			AdrSrc <= '0';
			ResultSrc <= "00";
			ALUSrcA <= '0';
			ALUSrcB <= "01";
			ALUOp <= '0';
		WHEN S3 =>
			Branch <= '0';
			RegW <= '0';
			MemW <= '0';
			IRWrite <= '0';
			NextPC <= '0';
			AdrSrc <= '1';
			ResultSrc <= "00";
			ALUSrcA <= '0';
			ALUSrcB <= "00";
			ALUOp <= '0';
		WHEN S4 =>
			Branch <= '0';
			RegW <= '1';
			MemW <= '0';
			IRWrite <= '0';
			NextPC <= '0';
			AdrSrc <= '0';
			ResultSrc <= "01";
			ALUSrcA <= '0';
			ALUSrcB <= "00";
			ALUOp <= '0';
		WHEN S5 =>
			Branch <= '0';
			RegW <= '0';
			MemW <= '1';
			IRWrite <= '0';
			NextPC <= '0';
			AdrSrc <= '1';
			ResultSrc <= "00";
			ALUSrcA <= '0';
			ALUSrcB <= "00";
			ALUOp <= '0';
		WHEN S6 =>
			Branch <= '0';
			RegW <= '0';
			MemW <= '0';
			IRWrite <= '0';
			NextPC <= '0';
			AdrSrc <= '0';
			ResultSrc <= "00";
			ALUSrcA <= '0';
			ALUSrcB <= "00";
			ALUOp <= '1';
		WHEN S7 =>
			Branch <= '0';
			RegW <= '0';
			MemW <= '0';
			IRWrite <= '0';
			NextPC <= '0';
			AdrSrc <= '0';
			ResultSrc <= "00";
			ALUSrcA <= '0';
			ALUSrcB <= "01";
			ALUOp <= '1';
		WHEN S8 =>
			Branch <= '0';
			RegW <= '1';
			MemW <= '0';
			IRWrite <= '0';
			NextPC <= '0';
			AdrSrc <= '0';
			ResultSrc <= "00";
			ALUSrcA <= '0';
			ALUSrcB <= "00";
			ALUOp <= '0';
		WHEN S9 =>
			Branch <= '1';
			RegW <= '0';
			MemW <= '0';
			IRWrite <= '0';
			NextPC <= '0';
			AdrSrc <= '0';
			ResultSrc <= "10";
			ALUSrcA <= '0';
			ALUSrcB <= "01";
			ALUOp <= '0';
	END CASE;
	END PROCESS;
	
	--Next state logic
	nextState <= S1 WHEN state=S0 ELSE
			   S2 WHEN (state=S1 AND Op="01") ELSE
			   S6 WHEN (state=S1 AND Op="00" AND Funct5='0') ELSE
			   S7 WHEN (state=S1 AND Op="00" AND Funct5='1') ELSE
			   S9 WHEN (state=S1 AND Op="10") ELSE
			   S3 WHEN (state=S2 AND Funct0='1') ELSE
			   S5 WHEN (state=S2 AND Funct0='0') ELSE
			   S8 WHEN (state=S6 OR state=S7) ELSE
			   S4 WHEN (state=S3) ELSE
			   S0;


END sim;
