// Logisim project ARM_Processor_Multicycle.circ as structural Verilog: 2 circuits, main circuit ARM_Processor_Multicycle
module ARM_Processor_Multicycle (
);

  wire arm_control_unit_multicycle_1_adrsrc, arm_control_unit_multicycle_1_alusrca,
       arm_control_unit_multicycle_1_irwrite, arm_control_unit_multicycle_1_memwrite,
       arm_control_unit_multicycle_1_pcwrite, arm_control_unit_multicycle_1_regwrite, Clk, not_1_out;
  wire [1:0] arm_control_unit_multicycle_1_alucontrol, arm_control_unit_multicycle_1_alusrcb,
       arm_control_unit_multicycle_1_immsrc, arm_control_unit_multicycle_1_regsrc,
       arm_control_unit_multicycle_1_resultsrc;
  wire [3:0] ALU_aluflags, multiplexer_2_out, multiplexer_3_out;
  wire [31:0] A_q, ALU_result, ALUOut_q, Data_q, Extend_extimm, Intructions_and_Data_dout, IR_q,
       multiplexer_1_out, multiplexer_4_out, multiplexer_5_out, multiplexer_6_out, PC_q, Register_File_rd1,
       Register_File_rd2, WriteData_q;

  Register #(.width(32)) PC (
    .D(multiplexer_6_out), .en(arm_control_unit_multicycle_1_pcwrite), .clk(Clk), .Q(PC_q));  // open: clr
  Clock u_Clk (.out(Clk));
  Multiplexer #(.width(32)) multiplexer_1 (
    .in0(PC_q), .in1(multiplexer_6_out), .out(multiplexer_1_out), .sel(arm_control_unit_multicycle_1_adrsrc));
  // Probe on multiplexer_1_out[9:2]
  RAM #(.asyncread("true"), .dataWidth(32), .\type ("nonvolatile")) Intructions_and_Data (
    .addr(multiplexer_1_out[9:2]), .we(arm_control_unit_multicycle_1_memwrite), .oe(not_1_out), .clk(Clk),
    .din(WriteData_q), .dout(Intructions_and_Data_dout));
  not not_1 (not_1_out, arm_control_unit_multicycle_1_memwrite);
  // Probe on Intructions_and_Data_dout
  Register #(.width(32)) IR (
    .D(Intructions_and_Data_dout), .en(arm_control_unit_multicycle_1_irwrite), .clk(Clk), .Q(IR_q));  // open: clr
  Register #(.width(32)) Data (.D(Intructions_and_Data_dout), .en(1'b1), .clk(Clk), .Q(Data_q));  // open: clr
  ARM_Control_Unit_Multicycle arm_control_unit_multicycle_1 (
    .Cond(IR_q[31:28]), .ALUFlags(ALU_aluflags), .Rd(IR_q[15:12]), .Op(IR_q[27:26]), .Funct(IR_q[25:20]),
    .Clk(Clk), .PCWrite(arm_control_unit_multicycle_1_pcwrite),
    .RegWrite(arm_control_unit_multicycle_1_regwrite), .MemWrite(arm_control_unit_multicycle_1_memwrite),
    .IRWrite(arm_control_unit_multicycle_1_irwrite), .AdrSrc(arm_control_unit_multicycle_1_adrsrc),
    .ResultSrc(arm_control_unit_multicycle_1_resultsrc), .ALUSrcA(arm_control_unit_multicycle_1_alusrca),
    .ALUSrcB(arm_control_unit_multicycle_1_alusrcb), .ALUControl(arm_control_unit_multicycle_1_alucontrol),
    .ImmSrc(arm_control_unit_multicycle_1_immsrc), .RegSrc(arm_control_unit_multicycle_1_regsrc));
  Multiplexer #(.width(4)) multiplexer_2 (
    .in0(IR_q[19:16]), .in1(4'b1111), .out(multiplexer_2_out), .sel(arm_control_unit_multicycle_1_regsrc[0]));
  Multiplexer #(.width(4)) multiplexer_3 (
    .in0(IR_q[3:0]), .in1(IR_q[15:12]), .out(multiplexer_3_out), .sel(arm_control_unit_multicycle_1_regsrc[1]));
  ARM_Register_File Register_File (
    .A1(multiplexer_2_out), .A2(multiplexer_3_out), .CLK(Clk), .WE3(arm_control_unit_multicycle_1_regwrite),
    .WD3(multiplexer_6_out), .A3(IR_q[15:12]), .R15(multiplexer_6_out), .RD1(Register_File_rd1),
    .RD2(Register_File_rd2));
  Register #(.width(32)) A (.D(Register_File_rd1), .en(1'b1), .clk(Clk), .Q(A_q));  // open: clr
  Register #(.width(32)) WriteData (.D(Register_File_rd2), .en(1'b1), .clk(Clk), .Q(WriteData_q));  // open: clr
  ARM_Extend Extend (.InstrImm(IR_q[23:0]), .ImmSrc(arm_control_unit_multicycle_1_immsrc), .ExtImm(Extend_extimm));
  // Probe on Extend_extimm
  Multiplexer #(.width(32)) multiplexer_4 (
    .in0(A_q), .in1(PC_q), .out(multiplexer_4_out), .sel(arm_control_unit_multicycle_1_alusrca));
  Multiplexer #(.select(2), .width(32)) multiplexer_5 (
    .in0(WriteData_q), .in1(Extend_extimm), .in2(32'h4), .out(multiplexer_5_out),
    .sel(arm_control_unit_multicycle_1_alusrcb));  // open: in3
  // Probe on ALU_aluflags
  // Probe on ALU_result
  ALU_32_bit ALU (
    .B(multiplexer_5_out), .A(multiplexer_4_out), .ALUControl(arm_control_unit_multicycle_1_alucontrol),
    .Result(ALU_result), .ALUFlags(ALU_aluflags));
  Register #(.width(32)) ALUOut (.D(ALU_result), .en(1'b1), .clk(Clk), .Q(ALUOut_q));  // open: clr
  Multiplexer #(.select(2), .width(32)) multiplexer_6 (
    .in0(ALUOut_q), .in1(Data_q), .in2(ALU_result), .out(multiplexer_6_out),
    .sel(arm_control_unit_multicycle_1_resultsrc));  // open: in3
  // Probe on multiplexer_6_out

  // Notes on the sheet:
  //   Memory unit uses 8-bit addresses to make things easier for now. Make sure PC doesn't go above that.
  //   It also uses word addressing instead of byte-addressing so the last 2 LSBs of the 32-bit byte addresses are dropped at the address inputs on the memory unit.
endmodule

module ARM_Shifter (
  input  [6:0] ctl,
  input  [31:0] X,
  output [31:0] Y
);

  // Probe on ctl[6:2]
  // Probe on ctl[1:0]

  assign Y = X;

  // Notes on the sheet:
  //   sh selects the different shift operation
  //   00 = LSL = Logical left shift
  //   01 = LSR = Logical right shift
  //   10 = ASR = Arithmetic shift right
  //   11 = ROR = Rotate right
  //   TODO: Implement this in VHDL as a 32-bit shifter is quite tedious to implement visually.
endmodule
