// Logisim project ARM_ALU.circ as structural Verilog: 6 circuits, main circuit ALU_32_bit
module Adder_1_bit (
  input  CarryIn,
  input  a,
  input  b,
  output CarryOut,
  output Sum
);

  wire and_1_out, and_2_out, and_3_out, and_4_out, and_5_out, and_6_out, and_7_out;

  and and_1 (and_1_out, CarryIn, a);
  and and_2 (and_2_out, CarryIn, b);
  and and_3 (and_3_out, a, b);
  and and_4 (and_4_out, a, ~b, ~CarryIn);  // AND_Gate
  and and_5 (and_5_out, ~a, b, ~CarryIn);  // AND_Gate
  and and_6 (and_6_out, ~a, ~b, CarryIn);  // AND_Gate
  and and_7 (and_7_out, a, b, CarryIn);
  or or_1 (CarryOut, and_1_out, and_2_out, and_3_out);
  or or_2 (Sum, and_4_out, and_5_out, and_6_out, and_7_out);
endmodule

module Mplex_3 (
  input  [1:0] S,
  input  A,
  input  B,
  input  C,
  output D
);

  wire and_1_out, and_2_out, and_3_out, and_4_out, and_5_out, and_6_out;

  and and_1 (and_1_out, ~S[1], ~S[0]);  // AND_Gate
  and and_2 (and_2_out, A, and_1_out);
  and and_3 (and_3_out, ~S[1], S[0]);  // AND_Gate
  and and_4 (and_4_out, S[1], ~S[0]);  // AND_Gate
  and and_5 (and_5_out, B, and_3_out);
  and and_6 (and_6_out, C, and_4_out);
  or or_1 (D, and_2_out, and_5_out, and_6_out);
endmodule

module ALU_1_bit (
  input  CarryIn,
  input  a,
  input  [1:0] Operation,
  input  b,
  output Result,
  output CarryOut
);

  wire adder_1_bit_1_sum, and_1_out, or_1_out;

  and and_1 (and_1_out, a, b);
  or or_1 (or_1_out, a, b);
  Adder_1_bit adder_1_bit_1 (.CarryIn(CarryIn), .a(a), .b(b), .CarryOut(CarryOut), .Sum(adder_1_bit_1_sum));
  Mplex_3 mplex_3_1 (.S(Operation), .A(and_1_out), .B(or_1_out), .C(adder_1_bit_1_sum), .D(Result));
endmodule

module ALU_32_bit (
  input  [1:0] ALUControl,
  input  [31:0] B,
  input  [31:0] A,
  output [31:0] Result,
  output [3:0] ALUFlags
);

  wire adder_32_bit_1_carryout, not_2_out, Sum31, xnor_1_out, xor_1_out;
  wire [30:0] adder_32_bit_1_sum;
  wire [31:0] and_1_out, multiplexer_1_out, not_1_out, or_1_out;

  assign not_1_out = ~B;  // NOT_Gate not_1, 32 bits wide
  Multiplexer #(.width(32)) multiplexer_1 (.in0(B), .in1(not_1_out), .out(multiplexer_1_out), .sel(ALUControl[0]));
  assign and_1_out = B & A;  // AND_Gate and_1, 32 bits wide
  assign or_1_out = B | A;  // OR_Gate or_1, 32 bits wide
  xor xor_1 (xor_1_out, Sum31, A[31]);
  NotExactlyOne xnor_1 (.out(xnor_1_out), .in0(A[31]), .in1(B[31]), .in2(ALUControl[0]));
  Adder_32_bit adder_32_bit_1 (
    .A(multiplexer_1_out), .B(A), .CarryIn(ALUControl[0]), .CarryOut(adder_32_bit_1_carryout),
    .Sum({Sum31, adder_32_bit_1_sum}));
  not not_2 (not_2_out, ALUControl[1]);
  Multiplexer #(.select(2), .width(32)) multiplexer_2 (
    .in0({Sum31, adder_32_bit_1_sum}), .in1({Sum31, adder_32_bit_1_sum}), .in2(and_1_out), .in3(or_1_out),
    .out({ALUFlags[3], Result[30:0]}), .sel(ALUControl));
  and and_2 (ALUFlags[1], adder_32_bit_1_carryout, not_2_out);
  and and_3 (ALUFlags[0], not_2_out, xor_1_out, xnor_1_out);
  Zero_Detect_32_bit Zero_Detect (.A({ALUFlags[3], Result[30:0]}), .B(ALUFlags[2]));

  assign Result[31] = ALUFlags[3];

  // Notes on the sheet:
  //   Negative
  //   Carry
  //   oVerflow
  //   Zero
  //   NZCV
endmodule

module Zero_Detect_32_bit (
  input  [31:0] A,
  output B
);

  nor nor_1 (B, A[0], A[1], A[2], A[3], A[4], A[5], A[6], A[7], A[8], A[9], A[10], A[11], A[12], A[13], A[14], A[15], A[16], A[17], A[18], A[19], A[20], A[21], A[22], A[23], A[24], A[25], A[26], A[27], A[28], A[29], A[30], A[31]);
endmodule

module Adder_32_bit (
  input  CarryIn,
  input  [31:0] A,
  input  [31:0] B,
  output [31:0] Sum,
  output CarryOut
);

  wire Bit_0_carryout, Bit_1_carryout, Bit_2_carryout, Bit_3_carryout, Bit_4_carryout, Bit_5_carryout,
       Bit_6_carryout, Bit_7_carryout, Bit_8_carryout, Bit_9_carryout, Bit_10_carryout, Bit_11_carryout,
       Bit_12_carryout, Bit_13_carryout, Bit_14_carryout, Bit_15_carryout, Bit_16_carryout, Bit_17_carryout,
       Bit_18_carryout, Bit_19_carryout, Bit_20_carryout, Bit_21_carryout, Bit_22_carryout, Bit_23_carryout,
       Bit_24_carryout, Bit_25_carryout, Bit_26_carryout, Bit_27_carryout, Bit_28_carryout, Bit_29_carryout,
       Bit_30_carryout;

  Adder_1_bit Bit_0 (.CarryIn(CarryIn), .a(A[0]), .b(B[0]), .CarryOut(Bit_0_carryout), .Sum(Sum[0]));
  Adder_1_bit Bit_1 (.CarryIn(Bit_0_carryout), .a(A[1]), .b(B[1]), .CarryOut(Bit_1_carryout), .Sum(Sum[1]));
  Adder_1_bit Bit_2 (.CarryIn(Bit_1_carryout), .a(A[2]), .b(B[2]), .CarryOut(Bit_2_carryout), .Sum(Sum[2]));
  Adder_1_bit Bit_3 (.CarryIn(Bit_2_carryout), .a(A[3]), .b(B[3]), .CarryOut(Bit_3_carryout), .Sum(Sum[3]));
  Adder_1_bit Bit_4 (.CarryIn(Bit_3_carryout), .a(A[4]), .b(B[4]), .CarryOut(Bit_4_carryout), .Sum(Sum[4]));
  Adder_1_bit Bit_5 (.CarryIn(Bit_4_carryout), .a(A[5]), .b(B[5]), .CarryOut(Bit_5_carryout), .Sum(Sum[5]));
  Adder_1_bit Bit_6 (.CarryIn(Bit_5_carryout), .a(A[6]), .b(B[6]), .CarryOut(Bit_6_carryout), .Sum(Sum[6]));
  Adder_1_bit Bit_7 (.CarryIn(Bit_6_carryout), .a(A[7]), .b(B[7]), .CarryOut(Bit_7_carryout), .Sum(Sum[7]));
  Adder_1_bit Bit_8 (.CarryIn(Bit_7_carryout), .a(A[8]), .b(B[8]), .CarryOut(Bit_8_carryout), .Sum(Sum[8]));
  Adder_1_bit Bit_9 (.CarryIn(Bit_8_carryout), .a(A[9]), .b(B[9]), .CarryOut(Bit_9_carryout), .Sum(Sum[9]));
  Adder_1_bit Bit_10 (.CarryIn(Bit_9_carryout), .a(A[10]), .b(B[10]), .CarryOut(Bit_10_carryout), .Sum(Sum[10]));
  Adder_1_bit Bit_11 (.CarryIn(Bit_10_carryout), .a(A[11]), .b(B[11]), .CarryOut(Bit_11_carryout), .Sum(Sum[11]));
  Adder_1_bit Bit_12 (.CarryIn(Bit_11_carryout), .a(A[12]), .b(B[12]), .CarryOut(Bit_12_carryout), .Sum(Sum[12]));
  Adder_1_bit Bit_13 (.CarryIn(Bit_12_carryout), .a(A[13]), .b(B[13]), .CarryOut(Bit_13_carryout), .Sum(Sum[13]));
  Adder_1_bit Bit_14 (.CarryIn(Bit_13_carryout), .a(A[14]), .b(B[14]), .CarryOut(Bit_14_carryout), .Sum(Sum[14]));
  Adder_1_bit Bit_15 (.CarryIn(Bit_14_carryout), .a(A[15]), .b(B[15]), .CarryOut(Bit_15_carryout), .Sum(Sum[15]));
  Adder_1_bit Bit_16 (.CarryIn(Bit_15_carryout), .a(A[16]), .b(B[16]), .CarryOut(Bit_16_carryout), .Sum(Sum[16]));
  Adder_1_bit Bit_17 (.CarryIn(Bit_16_carryout), .a(A[17]), .b(B[17]), .CarryOut(Bit_17_carryout), .Sum(Sum[17]));
  Adder_1_bit Bit_18 (.CarryIn(Bit_17_carryout), .a(A[18]), .b(B[18]), .CarryOut(Bit_18_carryout), .Sum(Sum[18]));
  Adder_1_bit Bit_19 (.CarryIn(Bit_18_carryout), .a(A[19]), .b(B[19]), .CarryOut(Bit_19_carryout), .Sum(Sum[19]));
  Adder_1_bit Bit_20 (.CarryIn(Bit_19_carryout), .a(A[20]), .b(B[20]), .CarryOut(Bit_20_carryout), .Sum(Sum[20]));
  Adder_1_bit Bit_21 (.CarryIn(Bit_20_carryout), .a(A[21]), .b(B[21]), .CarryOut(Bit_21_carryout), .Sum(Sum[21]));
  Adder_1_bit Bit_22 (.CarryIn(Bit_21_carryout), .a(A[22]), .b(B[22]), .CarryOut(Bit_22_carryout), .Sum(Sum[22]));
  Adder_1_bit Bit_23 (.CarryIn(Bit_22_carryout), .a(A[23]), .b(B[23]), .CarryOut(Bit_23_carryout), .Sum(Sum[23]));
  Adder_1_bit Bit_24 (.CarryIn(Bit_23_carryout), .a(A[24]), .b(B[24]), .CarryOut(Bit_24_carryout), .Sum(Sum[24]));
  Adder_1_bit Bit_25 (.CarryIn(Bit_24_carryout), .a(A[25]), .b(B[25]), .CarryOut(Bit_25_carryout), .Sum(Sum[25]));
  Adder_1_bit Bit_26 (.CarryIn(Bit_25_carryout), .a(A[26]), .b(B[26]), .CarryOut(Bit_26_carryout), .Sum(Sum[26]));
  Adder_1_bit Bit_27 (.CarryIn(Bit_26_carryout), .a(A[27]), .b(B[27]), .CarryOut(Bit_27_carryout), .Sum(Sum[27]));
  Adder_1_bit Bit_28 (.CarryIn(Bit_27_carryout), .a(A[28]), .b(B[28]), .CarryOut(Bit_28_carryout), .Sum(Sum[28]));
  Adder_1_bit Bit_29 (.CarryIn(Bit_28_carryout), .a(A[29]), .b(B[29]), .CarryOut(Bit_29_carryout), .Sum(Sum[29]));
  Adder_1_bit Bit_30 (.CarryIn(Bit_29_carryout), .a(A[30]), .b(B[30]), .CarryOut(Bit_30_carryout), .Sum(Sum[30]));
  Adder_1_bit Bit_31 (.CarryIn(Bit_30_carryout), .a(A[31]), .b(B[31]), .CarryOut(CarryOut), .Sum(Sum[31]));

  // Other names for the same wires on the sheet: A0[7:0] = A[7:0]; A1[7:0] = A[15:8]; A2[7:0] = A[23:16];
  //   A3[7:0] = A[31:24]; B0[7:0] = B[7:0]; B1[7:0] = B[15:8]; B2[7:0] = B[23:16]; B3[7:0] = B[31:24];
  //   S0[7:0] = Sum[7:0]; S1[7:0] = Sum[15:8]; S2[7:0] = Sum[23:16]; S3[7:0] = Sum[31:24]
endmodule
