// Logisim project ARM_Pipelined_Control.circ as structural Verilog: 7 circuits, main circuit ARM_Control_Unit
module ARM_PC_logic (
  input  [3:0] Rd,
  input  RegW,
  input  Branch,
  output PCS
);

  wire and_1_out, equality_4_bit_1_eq;

  Equality_4_bit equality_4_bit_1 (.A(4'b1111), .B(Rd), .EQ(equality_4_bit_1_eq));
  and and_1 (and_1_out, equality_4_bit_1_eq, RegW);
  or or_1 (PCS, and_1_out, Branch);

  // Notes on the sheet:
  //   PCS = ((Rd ==15) & RegW) | Branch
endmodule

module ARM_ALU_Decoder (
  input  ALUOp,
  input  [3:0] cmd,
  input  S,
  output [1:0] ALUControl,
  output [1:0] FlagW
);

  wire and_1_out, and_2_out, and_3_out, or_1_out, or_2_out, or_3_out;

  and and_1 (and_1_out, ~cmd[1], ~cmd[2]);  // AND_Gate
  and and_2 (and_2_out, ~cmd[1], cmd[3]);  // AND_Gate
  or or_1 (or_1_out, cmd[1], cmd[3]);
  or or_2 (or_2_out, and_1_out, and_2_out);
  and and_3 (and_3_out, cmd[2], ~cmd[3]);  // AND_Gate
  and and_4 (ALUControl[0], ALUOp, or_1_out);
  and and_5 (ALUControl[1], ALUOp, or_2_out);
  or or_3 (or_3_out, cmd[1], and_3_out);
  and and_6 (FlagW[1], ALUOp, S);
  and and_7 (FlagW[0], or_3_out, FlagW[1]);
endmodule

module Equality_4_bit (
  input  [3:0] A,
  input  [3:0] B,
  output EQ
);

  wire xnor_1_out, xnor_2_out, xnor_3_out, xnor_4_out;

  xnor xnor_1 (xnor_1_out, A[0], B[0]);
  xnor xnor_2 (xnor_2_out, A[1], B[1]);
  xnor xnor_3 (xnor_3_out, A[2], B[2]);
  xnor xnor_4 (xnor_4_out, A[3], B[3]);
  and and_1 (EQ, xnor_1_out, xnor_2_out, xnor_3_out, xnor_4_out);
endmodule

module ARM_Main_Decoder (
  input  [1:0] Op,
  input  Funct0,
  input  Funct5,
  output Branch,
  output MemToReg,
  output MemW,
  output ALUSrc,
  output [1:0] ImmSrc,
  output RegW,
  output [1:0] RegSrc,
  output ALUOp
);

  wire and_2_out, and_3_out, not_1_out, not_2_out, not_3_out;

  not not_1 (not_1_out, Op[1]);
  not not_2 (not_2_out, Op[0]);
  not not_3 (not_3_out, Funct0);
  and and_1 (MemW, Op[0], not_3_out);
  or or_1 (ALUSrc, Funct5, Op[0], Op[1]);
  and and_2 (and_2_out, not_1_out, not_2_out);
  and and_3 (and_3_out, not_1_out, Funct0);
  and and_4 (ALUOp, not_1_out, not_2_out);
  or or_2 (RegW, and_2_out, and_3_out);

  assign Branch = Op[1];
  assign ImmSrc = Op;
  assign MemToReg = Op[0];
  assign RegSrc = {Op[0], Op[1]};
endmodule

module ARM_Control_Unit (
  input  [3:0] Rd,
  input  [1:0] Op,
  input  [5:0] Funct,
  output PCSrcD,
  output BranchD,
  output MemToRegD,
  output MemWriteD,
  output ALUSrcD,
  output [1:0] ImmSrcD,
  output RegWriteD,
  output [1:0] RegSrcD,
  output [1:0] ALUControlD,
  output [1:0] FlagWriteD
);

  wire arm_main_decoder_1_aluop;

  ARM_Main_Decoder arm_main_decoder_1 (
    .Op(Op), .Funct0(Funct[0]), .Funct5(Funct[5]), .Branch(BranchD), .MemToReg(MemToRegD), .MemW(MemWriteD),
    .ALUSrc(ALUSrcD), .ImmSrc(ImmSrcD), .RegW(RegWriteD), .RegSrc(RegSrcD), .ALUOp(arm_main_decoder_1_aluop));
  ARM_PC_logic arm_pc_logic_1 (.Rd(Rd), .RegW(RegWriteD), .Branch(BranchD), .PCS(PCSrcD));
  ARM_ALU_Decoder arm_alu_decoder_1 (
    .ALUOp(arm_main_decoder_1_aluop), .cmd(Funct[4:1]), .S(Funct[0]), .ALUControl(ALUControlD),
    .FlagW(FlagWriteD));
endmodule

module ARM_Condition_Check (
  input  [3:0] Cond,
  input  [3:0] ALUFlags,
  output CondEx
);

  wire and_1_out, and_2_out, not_1_out, not_2_out, not_3_out, not_4_out, not_5_out, not_6_out, not_7_out,
       xor_1_out;

  xor xor_1 (xor_1_out, ALUFlags[3], ALUFlags[0]);
  and and_1 (and_1_out, ~ALUFlags[2], ALUFlags[1]);  // AND_Gate
  not not_1 (not_1_out, xor_1_out);
  and and_2 (and_2_out, not_1_out, ~ALUFlags[2]);  // AND_Gate
  not not_2 (not_2_out, ALUFlags[2]);
  not not_3 (not_3_out, ALUFlags[1]);
  not not_4 (not_4_out, ALUFlags[3]);
  not not_5 (not_5_out, ALUFlags[0]);
  not not_6 (not_6_out, and_1_out);
  not not_7 (not_7_out, and_2_out);
  Multiplexer #(.select(4)) multiplexer_1 (
    .in0(ALUFlags[2]), .in1(not_2_out), .in2(ALUFlags[1]), .in3(not_3_out), .in4(ALUFlags[3]),
    .in5(not_4_out), .in6(ALUFlags[0]), .in7(not_5_out), .in8(and_1_out), .in9(not_6_out), .in10(not_1_out),
    .in11(xor_1_out), .in12(and_2_out), .in13(not_7_out), .in14(1'b1), .out(CondEx), .sel(Cond));  // open: in15

  // Other names for the same wires on the sheet: V = ALUFlags[0]; C = ALUFlags[1]; Z = ALUFlags[2]; N = ALUFlags[3]

  // Notes on the sheet:
  //   Negative
  //   Zero
  //   Carry
  //   oVerflow
endmodule

module ARM_Conditional_Unit (
  input  [3:0] CondE,
  input  [1:0] FlagWriteE,
  input  [3:0] FlagsE,
  input  [3:0] ALUFlags,
  output CondEx,
  output [3:0] Flags_Out
);

  wire and_1_out, and_2_out;

  and and_1 (and_1_out, FlagWriteE[1], CondEx);
  Multiplexer #(.width(2)) multiplexer_1 (.in0(FlagsE[3:2]), .in1(ALUFlags[3:2]), .out(Flags_Out[3:2]));  // open: sel
  Multiplexer #(.width(2)) multiplexer_2 (
    .in0(FlagsE[1:0]), .in1(ALUFlags[1:0]), .out(Flags_Out[1:0]), .sel(and_2_out));
  and and_2 (and_2_out, FlagWriteE[0], CondEx);
  // Probe on Flags_Out[3:2]
  // Probe on Flags_Out[1:0]
  ARM_Condition_Check arm_condition_check_1 (.Cond(CondE), .ALUFlags(Flags_Out), .CondEx(CondEx));

  // Notes on the sheet:
  //   NZCV
  //   As compared to the single-cycle control, the state of the ALUFlags is maintained out side this functional unit in the FlagsE register.
  //   Accordingly, we select between the current ALU output and the previous ones via a multiplexer and send them out to be stored in the FlagsE register.
endmodule
