// Logisim project ARM_Processor_Pipelined.circ as structural Verilog: 10 circuits, main circuit ARM_Processor_Pipelined
module ARM_Processor_Pipelined (
);

  wire and_1_out, and_2_out, and_3_out, arm_conditional_unit_1_condex, arm_control_unit_1_alusrcd,
       arm_control_unit_1_branchd, arm_control_unit_1_memtoregd, arm_control_unit_1_memwrited,
       arm_control_unit_1_regwrited, arm_divider_decode_execute_1_alusrce,
       arm_divider_decode_execute_1_branche, arm_divider_decode_execute_1_memwritee,
       arm_divider_decode_execute_1_regwritee, arm_divider_execute_memory_1_memtoregm,
       arm_divider_execute_memory_1_memwritem, arm_divider_memory_writeback_1_memtoregw,
       arm_hazard_unit_clocked_1_cycletwo, arm_hazard_unit_clocked_1_flushd,
       arm_hazard_unit_clocked_1_flushe, arm_hazard_unit_clocked_1_stalld, arm_hazard_unit_clocked_1_stallf,
       BranchTakenE, CLK, Match_12_D_E, MemToRegE, not_1_out, PCSrcD, PCSrcE, PCSrcM, PCSrcW, RegWriteM,
       RegWriteW;
  wire [1:0] arm_control_unit_1_alucontrold, arm_control_unit_1_flagwrited, arm_control_unit_1_immsrcd,
       arm_control_unit_1_regsrcd, arm_divider_decode_execute_1_alucontrole,
       arm_divider_decode_execute_1_flagwritee, arm_hazard_unit_clocked_1_forwardae,
       arm_hazard_unit_clocked_1_forwardbe;
  wire [3:0] alu_32_bit_1_aluflags, arm_conditional_unit_1_flags_out, arm_divider_decode_execute_1_conde,
       arm_divider_decode_execute_1_flagse, arm_divider_decode_execute_1_ra1e,
       arm_divider_decode_execute_1_ra2e, arm_divider_decode_execute_1_wa3e,
       arm_divider_execute_memory_1_wa3m, arm_divider_memory_writeback_1_wa3w, Match_E, multiplexer_3_out,
       multiplexer_4_out;
  wire [31:0] adder_1_out, alu_32_bit_1_result, arm_divider_decode_execute_1_extimme,
       arm_divider_decode_execute_1_rd1e, arm_divider_decode_execute_1_rd2e,
       arm_divider_execute_memory_1_aluoutm, arm_divider_execute_memory_1_writedatam,
       arm_divider_fetch_decode_1_instrd, arm_divider_memory_writeback_1_aluoutw,
       arm_divider_memory_writeback_1_readdataw, arm_extend_1_extimm, Data_dout, Instructions_data,
       multiplexer_1_out, multiplexer_2_out, multiplexer_5_out, multiplexer_6_out, multiplexer_7_out,
       multiplexer_8_out, PC_q, registerfile_1_rd1, registerfile_1_rd2;

  Multiplexer #(.width(32)) multiplexer_1 (
    .in0(adder_1_out), .in1(multiplexer_8_out), .out(multiplexer_1_out));  // open: sel
  Multiplexer #(.width(32)) multiplexer_2 (
    .in0(multiplexer_1_out), .in1(alu_32_bit_1_result), .out(multiplexer_2_out));  // open: sel
  not not_1 (not_1_out, arm_hazard_unit_clocked_1_stallf);
  Register #(.width(32)) PC (.D(multiplexer_2_out), .en(not_1_out), .clk(CLK), .Q(PC_q));  // open: clr
  Clock #(.phaseOffset(1)) u_CLK (.out(CLK));
  ROM #(.dataWidth(32)) Instructions (.addr(PC_q[9:2]), .data(Instructions_data));
  Adder #(.width(32)) adder_1 (.a(PC_q), .b(32'h4), .out(adder_1_out));  // open: cin, cout
  ARM_Divider_Fetch_Decode arm_divider_fetch_decode_1 (
    .InstrF(Instructions_data), .En(arm_hazard_unit_clocked_1_stalld), .Clk(CLK),
    .Clr(arm_hazard_unit_clocked_1_flushd), .InstrD(arm_divider_fetch_decode_1_instrd));
  // Probe on adder_1_out
  ARM_Control_Unit arm_control_unit_1 (
    .Rd(arm_divider_fetch_decode_1_instrd[15:12]), .Op(arm_divider_fetch_decode_1_instrd[27:26]),
    .Funct(arm_divider_fetch_decode_1_instrd[25:20]), .PCSrcD(PCSrcD), .BranchD(arm_control_unit_1_branchd),
    .MemToRegD(arm_control_unit_1_memtoregd), .MemWriteD(arm_control_unit_1_memwrited),
    .ALUSrcD(arm_control_unit_1_alusrcd), .ImmSrcD(arm_control_unit_1_immsrcd),
    .RegWriteD(arm_control_unit_1_regwrited), .RegSrcD(arm_control_unit_1_regsrcd),
    .ALUControlD(arm_control_unit_1_alucontrold), .FlagWriteD(arm_control_unit_1_flagwrited));
  Multiplexer #(.width(4)) multiplexer_3 (
    .in0(arm_divider_fetch_decode_1_instrd[19:16]), .in1(4'b1111), .out(multiplexer_3_out));  // open: sel
  Multiplexer #(.width(4)) multiplexer_4 (
    .in0(arm_divider_fetch_decode_1_instrd[3:0]), .in1(arm_divider_fetch_decode_1_instrd[15:12]),
    .out(multiplexer_4_out));  // open: sel
  RegisterFile registerfile_1 (
    .A1(multiplexer_3_out), .A2(multiplexer_4_out), .CLK(CLK), .WE3(RegWriteW), .WD3(multiplexer_8_out),
    .A3(arm_divider_memory_writeback_1_wa3w), .R15(adder_1_out), .RD1(registerfile_1_rd1),
    .RD2(registerfile_1_rd2));
  ARM_Extend arm_extend_1 (
    .InstrImm(arm_divider_fetch_decode_1_instrd[23:0]), .ImmSrc(arm_control_unit_1_immsrcd),
    .ExtImm(arm_extend_1_extimm));
  ARM_Match_12D_E arm_match_12d_e_1 (
    .RA1D(multiplexer_3_out), .RA2D(multiplexer_4_out), .WA3E(arm_divider_decode_execute_1_wa3e),
    .Match_12D_E(Match_12_D_E));
  ARM_Divider_Decode_Execute arm_divider_decode_execute_1 (
    .CLK(CLK), .RD1D(registerfile_1_rd1), .RD2D(registerfile_1_rd2), .ExtImmD(arm_extend_1_extimm),
    .WA3D(arm_divider_fetch_decode_1_instrd[15:12]), .CLR(arm_hazard_unit_clocked_1_flushe),
    .RA1D(multiplexer_3_out), .RA2D(multiplexer_4_out), .PCSrcD(PCSrcD),
    .RegWriteD(arm_control_unit_1_regwrited), .MemToRegD(arm_control_unit_1_memtoregd),
    .MemWriteD(arm_control_unit_1_memwrited), .ALUControlD(arm_control_unit_1_alucontrold),
    .BranchD(arm_control_unit_1_branchd), .ALUSrcD(arm_control_unit_1_alusrcd),
    .FlagWriteD(arm_control_unit_1_flagwrited), .CondD(arm_divider_fetch_decode_1_instrd[31:28]),
    .FlagsD(arm_conditional_unit_1_flags_out), .RD1E(arm_divider_decode_execute_1_rd1e),
    .RD2E(arm_divider_decode_execute_1_rd2e), .ExtImmE(arm_divider_decode_execute_1_extimme),
    .WA3E(arm_divider_decode_execute_1_wa3e), .RA1E(arm_divider_decode_execute_1_ra1e),
    .RA2E(arm_divider_decode_execute_1_ra2e), .PCSrcE(PCSrcE),
    .RegWriteE(arm_divider_decode_execute_1_regwritee), .MemToRegE(MemToRegE),
    .MemWriteE(arm_divider_decode_execute_1_memwritee),
    .ALUControlE(arm_divider_decode_execute_1_alucontrole), .BranchE(arm_divider_decode_execute_1_branche),
    .ALUSrcE(arm_divider_decode_execute_1_alusrce), .FlagWriteE(arm_divider_decode_execute_1_flagwritee),
    .CondE(arm_divider_decode_execute_1_conde), .FlagsE(arm_divider_decode_execute_1_flagse));
  Multiplexer #(.select(2), .width(32)) multiplexer_5 (
    .in0(arm_divider_decode_execute_1_rd1e), .in1(multiplexer_8_out),
    .in2(arm_divider_execute_memory_1_aluoutm), .out(multiplexer_5_out),
    .sel(arm_hazard_unit_clocked_1_forwardae));  // open: in3
  Multiplexer #(.select(2), .width(32)) multiplexer_6 (
    .in0(arm_divider_decode_execute_1_rd2e), .in1(multiplexer_8_out),
    .in2(arm_divider_execute_memory_1_aluoutm), .out(multiplexer_6_out),
    .sel(arm_hazard_unit_clocked_1_forwardbe));  // open: in3
  Multiplexer #(.width(32)) multiplexer_7 (
    .in0(multiplexer_6_out), .in1(arm_divider_decode_execute_1_extimme), .out(multiplexer_7_out));  // open: sel
  ARM_Hazard_Unit_Clocked arm_hazard_unit_clocked_1 (
    .PCSrcW(PCSrcW), .BranchTakenE(BranchTakenE), .CLK(CLK), .Match_12_D_E(Match_12_D_E), .Match_E(Match_E),
    .RegWriteM(RegWriteM), .RegWriteW(RegWriteW), .MemToRegE(MemToRegE), .PCSrcD(PCSrcD), .PCSrcE(PCSrcE),
    .PCSrcM(PCSrcM), .ForwardAE(arm_hazard_unit_clocked_1_forwardae),
    .ForwardBE(arm_hazard_unit_clocked_1_forwardbe), .FlushE(arm_hazard_unit_clocked_1_flushe),
    .StallF(arm_hazard_unit_clocked_1_stallf), .StallD(arm_hazard_unit_clocked_1_stalld),
    .CycleTwo(arm_hazard_unit_clocked_1_cycletwo), .FlushD(arm_hazard_unit_clocked_1_flushd));
  ALU_32_bit alu_32_bit_1 (
    .B(multiplexer_7_out), .A(multiplexer_5_out), .ALUControl(arm_divider_decode_execute_1_alucontrole),
    .Result(alu_32_bit_1_result), .ALUFlags(alu_32_bit_1_aluflags));
  and and_1 (and_1_out, PCSrcE, arm_conditional_unit_1_condex);
  and and_2 (and_2_out, arm_divider_decode_execute_1_regwritee, arm_conditional_unit_1_condex);
  and and_3 (and_3_out, arm_divider_decode_execute_1_memwritee, arm_conditional_unit_1_condex);
  and and_4 (BranchTakenE, arm_divider_decode_execute_1_branche, arm_conditional_unit_1_condex);
  ARM_Conditional_Unit arm_conditional_unit_1 (
    .FlagWriteE(arm_divider_decode_execute_1_flagwritee), .CondE(arm_divider_decode_execute_1_conde),
    .FlagsE(arm_divider_decode_execute_1_flagse), .ALUFlags(alu_32_bit_1_aluflags),
    .CondEx(arm_conditional_unit_1_condex), .Flags_Out(arm_conditional_unit_1_flags_out));
  ARM_Match_E arm_match_e_1 (
    .RA1E(arm_divider_decode_execute_1_ra1e), .RA2E(arm_divider_decode_execute_1_ra2e),
    .WA3M(arm_divider_execute_memory_1_wa3m), .WA3W(arm_divider_memory_writeback_1_wa3w), .Match_E(Match_E));
  ARM_Divider_Execute_Memory arm_divider_execute_memory_1 (
    .CycleTwo(arm_hazard_unit_clocked_1_cycletwo), .CLK(CLK), .PCSrcE(and_1_out), .RegWriteE(and_2_out),
    .MemToRegE(MemToRegE), .MemWriteE(and_3_out), .ALUResultE(alu_32_bit_1_result),
    .WriteDataE(multiplexer_6_out), .WA3E(arm_divider_decode_execute_1_wa3e), .PCSrcM(PCSrcM),
    .RegWriteM(RegWriteM), .MemToRegM(arm_divider_execute_memory_1_memtoregm),
    .MemWriteM(arm_divider_execute_memory_1_memwritem), .ALUOutM(arm_divider_execute_memory_1_aluoutm),
    .WriteDataM(arm_divider_execute_memory_1_writedatam), .WA3M(arm_divider_execute_memory_1_wa3m));
  RAM #(.dataWidth(32), .enables("line"), .\type ("nonvolatile")) Data (
    .addr(arm_divider_execute_memory_1_aluoutm[9:2]), .we(arm_divider_execute_memory_1_memwritem), .clk(CLK),
    .din(arm_divider_execute_memory_1_writedatam), .dout(Data_dout));
  ARM_Divider_Memory_Writeback arm_divider_memory_writeback_1 (
    .CLK(CLK), .PCSrcM(PCSrcM), .RegWriteM(RegWriteM), .MemToRegM(arm_divider_execute_memory_1_memtoregm),
    .ReadDataM(Data_dout), .ALUOutE(arm_divider_execute_memory_1_aluoutm),
    .WA3M(arm_divider_execute_memory_1_wa3m), .PCSrcW(PCSrcW), .RegWriteW(RegWriteW),
    .MemToRegW(arm_divider_memory_writeback_1_memtoregw),
    .ReadDataW(arm_divider_memory_writeback_1_readdataw), .ALUOutW(arm_divider_memory_writeback_1_aluoutw),
    .WA3W(arm_divider_memory_writeback_1_wa3w));
  Multiplexer #(.width(32)) multiplexer_8 (
    .in0(arm_divider_memory_writeback_1_aluoutw), .in1(arm_divider_memory_writeback_1_readdataw),
    .out(multiplexer_8_out));  // open: sel
  // Probe on multiplexer_8_out

  // Notes on the sheet:
  //   contents of Instructions (hex, n*v repeats v):
  //   e4102008 e089300a e0414005 e00c500d e4016007 e38b702a
  //   Memory units use 8-bit addresses to make things easier for now. Make sure PC doesn't go above that.
  //   They also use word addressing instead of byte-addressing so constants the last 2 LSBs of the 32-bit byte addresses are dropped at the address inputs on the memory units.
endmodule

module ARM_Divider_Fetch_Decode (
  input  [31:0] InstrF,
  input  En,
  input  Clr,
  input  Clk,
  output [31:0] InstrD
);

  wire buffer_1_out, buffer_2_out, buffer_3_out, buffer_4_out, buffer_5_out, buffer_6_out, buffer_7_out,
       not_1_out;

  not not_1 (not_1_out, En);
  Register #(.width(32)) Instr (.D(InstrF), .en(not_1_out), .clk(buffer_1_out), .Q(InstrD), .clr(Clr));
  buf buffer_1 (buffer_1_out, buffer_2_out);
  buf buffer_2 (buffer_2_out, buffer_3_out);
  buf buffer_3 (buffer_3_out, buffer_4_out);
  buf buffer_4 (buffer_4_out, buffer_5_out);
  buf buffer_5 (buffer_5_out, buffer_6_out);
  buf buffer_6 (buffer_6_out, buffer_7_out);
  buf buffer_7 (buffer_7_out, Clk);
endmodule

module ARM_Divider_Decode_Execute (
  input  PCSrcD,
  input  BranchD,
  input  [31:0] RD1D,
  input  [3:0] RA1D,
  input  RegWriteD,
  input  ALUSrcD,
  input  [31:0] RD2D,
  input  [3:0] RA2D,
  input  MemToRegD,
  input  [1:0] FlagWriteD,
  input  [31:0] ExtImmD,
  input  MemWriteD,
  input  [3:0] CondD,
  input  [3:0] WA3D,
  input  [1:0] ALUControlD,
  input  [3:0] FlagsD,
  input  CLK,
  input  CLR,
  output PCSrcE,
  output BranchE,
  output [31:0] RD1E,
  output [3:0] RA1E,
  output RegWriteE,
  output ALUSrcE,
  output [31:0] RD2E,
  output [3:0] RA2E,
  output MemToRegE,
  output [1:0] FlagWriteE,
  output [31:0] ExtImmE,
  output MemWriteE,
  output [3:0] CondE,
  output [3:0] WA3E,
  output [1:0] ALUControlE,
  output [3:0] FlagsE
);

  Register #(.width(1)) PCSrc (.D(PCSrcD), .en(1'b1), .clk(CLK), .Q(PCSrcE), .clr(CLR));
  Register #(.width(1)) RegWrite (.D(RegWriteD), .en(1'b1), .clk(CLK), .Q(RegWriteE), .clr(CLR));
  Register #(.width(1)) MemToReg (.D(MemToRegD), .en(1'b1), .clk(CLK), .Q(MemToRegE), .clr(CLR));
  Register #(.width(1)) MemWrite (.D(MemWriteD), .en(1'b1), .clk(CLK), .Q(MemWriteE), .clr(CLR));
  Register #(.width(2)) ALUControl (.D(ALUControlD), .en(1'b1), .clk(CLK), .Q(ALUControlE), .clr(CLR));
  Register #(.width(1)) Branch (.D(BranchD), .en(1'b1), .clk(CLK), .Q(BranchE), .clr(CLR));
  Register #(.width(1)) ALUSrc (.D(ALUSrcD), .en(1'b1), .clk(CLK), .Q(ALUSrcE), .clr(CLR));
  Register #(.width(2)) FlagWrite (.D(FlagWriteD), .en(1'b1), .clk(CLK), .Q(FlagWriteE), .clr(CLR));
  Register #(.width(4)) Cond (.D(CondD), .en(1'b1), .clk(CLK), .Q(CondE), .clr(CLR));
  Register #(.width(4)) Flags (.D(FlagsD), .en(1'b1), .clk(CLK), .Q(FlagsE), .clr(CLR));
  Register #(.width(32)) RD1 (.D(RD1D), .en(1'b1), .clk(CLK), .Q(RD1E), .clr(CLR));
  Register #(.width(32)) RD2 (.D(RD2D), .en(1'b1), .clk(CLK), .Q(RD2E), .clr(CLR));
  Register #(.width(32)) ExtImm (.D(ExtImmD), .en(1'b1), .clk(CLK), .Q(ExtImmE), .clr(CLR));
  Register #(.width(4)) WA3 (.D(WA3D), .en(1'b1), .clk(CLK), .Q(WA3E), .clr(CLR));
  Register #(.width(4)) RA1 (.D(RA1D), .en(1'b1), .clk(CLK), .Q(RA1E), .clr(CLR));
  Register #(.width(4)) RA2 (.D(RA2D), .en(1'b1), .clk(CLK), .Q(RA2E), .clr(CLR));

  // Notes on the sheet:
  //   Control
  //   Data
  //   Inputs
endmodule

module ARM_Divider_Execute_Memory (
  input  CycleTwo,
  input  CLK,
  input  PCSrcE,
  input  [31:0] ALUResultE,
  input  RegWriteE,
  input  [31:0] WriteDataE,
  input  MemToRegE,
  input  [3:0] WA3E,
  input  MemWriteE,
  output PCSrcM,
  output [31:0] ALUOutM,
  output RegWriteM,
  output [31:0] WriteDataM,
  output MemToRegM,
  output [3:0] WA3M,
  output MemWriteM
);

  wire CLK_t, CLR;

  Register #(.width(1)) PCSrc (.D(PCSrcE), .en(1'b1), .clk(CLK_t), .Q(PCSrcM), .clr(CLR));
  Register #(.width(1)) RegWrite (.D(RegWriteE), .en(1'b1), .clk(CLK_t), .Q(RegWriteM), .clr(CLR));
  Register #(.width(1)) MemToReg (.D(MemToRegE), .en(1'b1), .clk(CLK_t), .Q(MemToRegM), .clr(CLR));
  Register #(.width(1)) MemWrite (.D(MemWriteE), .en(1'b1), .clk(CLK_t), .Q(MemWriteM), .clr(CLR));
  Register #(.width(32)) ALUResult (.D(ALUResultE), .en(1'b1), .clk(CLK_t), .Q(ALUOutM), .clr(CLR));
  Register #(.width(32)) WriteData (.D(WriteDataE), .en(1'b1), .clk(CLK_t), .Q(WriteDataM), .clr(CLR));
  Register #(.width(4)) WA3 (.D(WA3E), .en(1'b1), .clk(CLK_t), .Q(WA3M), .clr(CLR));
  Multiplexer multiplexer_1 (.in0(1'b1), .in1(CLK), .out(CLK_t));  // open: sel

  // Notes on the sheet:
  //   Control
  //   Data
  //   The CycleTwo input is a hack to eliminate an initialization issue involving undefined signals when the system is reset.
endmodule

module ARM_Divider_Memory_Writeback (
  input  CLK,
  input  PCSrcM,
  input  [31:0] ReadDataM,
  input  RegWriteM,
  input  [31:0] ALUOutE,
  input  MemToRegM,
  input  [3:0] WA3M,
  output PCSrcW,
  output [31:0] ReadDataW,
  output RegWriteW,
  output [31:0] ALUOutW,
  output MemToRegW,
  output [3:0] WA3W
);

  wire CLR;

  Register #(.width(1)) PCSrc (.D(PCSrcM), .en(1'b1), .clk(CLK), .Q(PCSrcW), .clr(CLR));
  Register #(.width(1)) RegWrite (.D(RegWriteM), .en(1'b1), .clk(CLK), .Q(RegWriteW), .clr(CLR));
  Register #(.width(1)) MemToReg (.D(MemToRegM), .en(1'b1), .clk(CLK), .Q(MemToRegW), .clr(CLR));
  Register #(.width(32)) ReadData (.D(ReadDataM), .en(1'b1), .clk(CLK), .Q(ReadDataW), .clr(CLR));
  Register #(.width(32)) ALUOut (.D(ALUOutE), .en(1'b1), .clk(CLK), .Q(ALUOutW), .clr(CLR));
  Register #(.width(4)) WA3 (.D(WA3M), .en(1'b1), .clk(CLK), .Q(WA3W), .clr(CLR));

  // Notes on the sheet:
  //   Control
  //   Data
endmodule

module ARM_Hazard_Unit (
  input  MemToRegE,
  input  Match_12_D_E,
  input  PCSrcD,
  input  PCSrcE,
  input  PCSrcM,
  input  BranchTakenE,
  input  PCSrcW,
  input  RegWriteM,
  input  RegWriteW,
  input  [3:0] Match_E,
  output StallD,
  output StallF,
  output FlushE,
  output FlushD,
  output [1:0] ForwardAE,
  output [1:0] ForwardBE
);

  wire or_1_out;

  and and_1 (StallD, MemToRegE, Match_12_D_E);
  or or_1 (or_1_out, PCSrcD, PCSrcE, PCSrcM);
  // Probe on StallD
  // Probe on or_1_out
  or or_2 (StallF, StallD, or_1_out);
  or or_3 (FlushE, StallD, BranchTakenE);
  or or_4 (FlushD, or_1_out, PCSrcW, BranchTakenE);
  ARM_Forward_xE arm_forward_xe_1 (
    .RegWriteM(RegWriteM), .Match_XE_M(Match_E[0]), .RegWriteW(RegWriteW), .Match_XE_W(Match_E[1]),
    .FowardXE(ForwardAE));
  ARM_Forward_xE arm_forward_xe_2 (
    .RegWriteM(RegWriteM), .Match_XE_M(Match_E[2]), .RegWriteW(RegWriteW), .Match_XE_W(Match_E[3]),
    .FowardXE(ForwardBE));

  // Notes on the sheet:
  //   Match_1E_M
  //   Match_1E_W
  //   Match_2E_M
  //   Match_2E_W
endmodule

module ARM_Match_E (
  input  [3:0] RA1E,
  input  [3:0] RA2E,
  input  [3:0] WA3M,
  input  [3:0] WA3W,
  output [3:0] Match_E
);

  Equality_4_bit equality_4_bit_1 (.A(RA1E), .B(WA3M), .EQ(Match_E[0]));
  Equality_4_bit equality_4_bit_2 (.A(RA1E), .B(WA3W), .EQ(Match_E[1]));
  Equality_4_bit equality_4_bit_3 (.A(RA2E), .B(WA3M), .EQ(Match_E[2]));
  Equality_4_bit equality_4_bit_4 (.A(RA2E), .B(WA3W), .EQ(Match_E[3]));

  // Notes on the sheet:
  //   Match_1E_M
  //   Match_1E_W
  //   Match_2E_M
  //   Match_2E_W
endmodule

module ARM_Match_12D_E (
  input  [3:0] RA1D,
  input  [3:0] RA2D,
  input  [3:0] WA3E,
  output Match_12D_E
);

  wire equality_4_bit_1_eq, equality_4_bit_2_eq;

  Equality_4_bit equality_4_bit_1 (.A(RA1D), .B(WA3E), .EQ(equality_4_bit_1_eq));
  Equality_4_bit equality_4_bit_2 (.A(RA2D), .B(WA3E), .EQ(equality_4_bit_2_eq));
  or or_1 (Match_12D_E, equality_4_bit_1_eq, equality_4_bit_2_eq);
endmodule

module ARM_Forward_xE (
  input  RegWriteM,
  input  Match_XE_M,
  input  RegWriteW,
  input  Match_XE_W,
  output [1:0] FowardXE
);

  wire and_1_out, and_2_out;
  wire [1:0] multiplexer_1_out;

  and and_1 (and_1_out, RegWriteM, Match_XE_M);
  and and_2 (and_2_out, RegWriteW, Match_XE_W);
  Multiplexer #(.width(2)) multiplexer_1 (.in0(2'b00), .in1(2'b01), .out(multiplexer_1_out));  // open: sel
  Multiplexer #(.width(2)) multiplexer_2 (.in0(multiplexer_1_out), .in1(2'b10), .out(FowardXE));  // open: sel
endmodule

module ARM_Hazard_Unit_Clocked (
  input  RegWriteM,
  input  RegWriteW,
  input  MemToRegE,
  input  PCSrcD,
  input  PCSrcE,
  input  PCSrcM,
  input  PCSrcW,
  input  BranchTakenE,
  input  Match_12_D_E,
  input  [3:0] Match_E,
  input  CLK,
  output FlushD,
  output StallF,
  output StallD,
  output FlushE,
  output [1:0] ForwardAE,
  output [1:0] ForwardBE,
  output CycleTwo
);

  wire and_5_out, arm_hazard_unit_1_flushd, arm_hazard_unit_1_flushe, arm_hazard_unit_1_stalld,
       arm_hazard_unit_1_stallf, buffer_1_out, buffer_2_out, buffer_3_out, buffer_4_out, buffer_5_out,
       d_ff_3_q, d_ff_5_q, d_ff_6_q, equality_4_bit_1_eq, equality_4_bit_2_eq, equality_4_bit_3_eq, or_2_out;
  wire [3:0] and_4_out, Valid_Hazards_q;

  D_Flip_Flop #(.trigger("falling")) d_ff_1 (
    .D(arm_hazard_unit_1_stallf), .clk(CLK), .Q(StallF));  // open: Qn, preset, reset
  and and_1 (and_4_out[2], Match_E[2], or_2_out);
  and and_2 (and_4_out[1], Match_E[1], equality_4_bit_3_eq);
  and and_3 (and_4_out[3], Match_E[3], equality_4_bit_3_eq);
  and and_4 (and_4_out[0], Match_E[0], or_2_out);
  Counter #(.max('h4), .ongoal("stay"), .width(4)) Valid_Hazards (
    .up(1'b1), .count(1'b1), .clk(CLK), .Q(Valid_Hazards_q));  // open: clr, load, D, carry
  and and_5 (and_5_out, Match_12_D_E, CycleTwo);
  D_Flip_Flop #(.trigger("falling")) d_ff_2 (
    .D(arm_hazard_unit_1_stalld), .clk(CLK), .Q(StallD));  // open: Qn, preset, reset
  D_Flip_Flop #(.trigger("falling")) d_ff_3 (
    .D(arm_hazard_unit_1_flushd), .clk(CLK), .Q(d_ff_3_q));  // open: Qn, preset, reset
  Equality_4_bit equality_4_bit_1 (.A(Valid_Hazards_q), .B(4'b0010), .EQ(equality_4_bit_1_eq));
  Equality_4_bit equality_4_bit_2 (.A(Valid_Hazards_q), .B(4'b0011), .EQ(equality_4_bit_2_eq));
  Equality_4_bit equality_4_bit_3 (.A(Valid_Hazards_q), .B(4'b0100), .EQ(equality_4_bit_3_eq));
  D_Flip_Flop d_ff_4 (.D(d_ff_3_q), .clk(CLK), .Q(FlushD));  // open: Qn, preset, reset
  or or_1 (CycleTwo, equality_4_bit_1_eq, equality_4_bit_2_eq, equality_4_bit_3_eq);
  or or_2 (or_2_out, equality_4_bit_2_eq, equality_4_bit_3_eq);
  D_Flip_Flop #(.trigger("falling")) d_ff_5 (
    .D(arm_hazard_unit_1_flushe), .clk(CLK), .Q(d_ff_5_q));  // open: Qn, preset, reset
  D_Flip_Flop d_ff_6 (.D(d_ff_5_q), .clk(CLK), .Q(d_ff_6_q));  // open: Qn, preset, reset
  buf buffer_1 (buffer_1_out, CLK);
  buf buffer_2 (buffer_2_out, buffer_1_out);
  buf buffer_3 (buffer_3_out, buffer_2_out);
  buf buffer_4 (buffer_4_out, buffer_3_out);
  buf buffer_5 (buffer_5_out, buffer_4_out);
  ARM_Hazard_Unit arm_hazard_unit_1 (
    .Match_E(and_4_out), .Match_12_D_E(and_5_out), .PCSrcD(PCSrcD), .PCSrcE(PCSrcE), .PCSrcM(PCSrcM),
    .BranchTakenE(BranchTakenE), .PCSrcW(PCSrcW), .MemToRegE(MemToRegE), .RegWriteM(RegWriteM),
    .RegWriteW(RegWriteW), .StallF(arm_hazard_unit_1_stallf), .FlushE(arm_hazard_unit_1_flushe),
    .StallD(arm_hazard_unit_1_stalld), .FlushD(arm_hazard_unit_1_flushd), .ForwardAE(ForwardAE),
    .ForwardBE(ForwardBE));
  and and_6 (FlushE, d_ff_6_q, buffer_5_out);

  // Notes on the sheet:
  //   Match_1E_M
  //   Match_1E_W
  //   Match_2E_M
  //   Match_2E_W
  //   <=2
  //   <=3
  //   ==4
endmodule
