// Logisim project ARM_Register_File_Pipelined.circ as structural Verilog
module RegisterFile (
  input  CLK,
  input  WE3,
  input  [31:0] WD3,
  input  [31:0] R15,
  input  [3:0] A1,
  input  [3:0] A2,
  input  [3:0] A3,
  output [31:0] RD1,
  output [31:0] RD2
);

  wire and_1_out, and_2_out, and_3_out, and_4_out, and_5_out, and_6_out, and_7_out, and_8_out, and_9_out,
       and_10_out, and_11_out, and_12_out, and_13_out, and_14_out, and_15_out, Dec0, Dec1, Dec2, Dec3, Dec4,
       Dec5, Dec6, Dec7, Dec8, Dec9, Dec10, Dec11, Dec12, Dec13, Dec14;
  wire [31:0] R0, R1, R2, R3, R4, R5, R6, R7, R8, R9, R10, R11, R12, R13, R14;

  Decoder #(.enable("false"), .select(4)) decoder_1 (
    .out0(Dec0), .out1(Dec1), .out2(Dec2), .out3(Dec3), .out4(Dec4), .out5(Dec5), .out6(Dec6), .out7(Dec7),
    .out8(Dec8), .out9(Dec9), .out10(Dec10), .out11(Dec11), .out12(Dec12), .out13(Dec13), .out14(Dec14),
    .sel(A3));  // open: out15
  Register #(.trigger("falling"), .width(32)) u_R0 (.D(WD3), .en(and_1_out), .clk(CLK), .Q(R0));  // open: clr
  and and_1 (and_1_out, Dec0, WE3);
  Register #(.trigger("falling"), .width(32)) u_R1 (.D(WD3), .en(and_2_out), .clk(CLK), .Q(R1));  // open: clr
  and and_2 (and_2_out, Dec1, WE3);
  Register #(.trigger("falling"), .width(32)) u_R2 (.D(WD3), .en(and_3_out), .clk(CLK), .Q(R2));  // open: clr
  and and_3 (and_3_out, Dec2, WE3);
  Register #(.trigger("falling"), .width(32)) u_R3 (.D(WD3), .en(and_4_out), .clk(CLK), .Q(R3));  // open: clr
  and and_4 (and_4_out, Dec3, WE3);
  Register #(.trigger("falling"), .width(32)) u_R4 (.D(WD3), .en(and_5_out), .clk(CLK), .Q(R4));  // open: clr
  and and_5 (and_5_out, Dec4, WE3);
  and and_6 (and_6_out, Dec5, WE3);
  and and_7 (and_7_out, Dec6, WE3);
  and and_8 (and_8_out, Dec7, WE3);
  and and_9 (and_9_out, Dec8, WE3);
  and and_10 (and_10_out, Dec9, WE3);
  Register #(.trigger("falling"), .width(32)) u_R5 (.D(WD3), .en(and_6_out), .clk(CLK), .Q(R5));  // open: clr
  Register #(.trigger("falling"), .width(32)) u_R6 (.D(WD3), .en(and_7_out), .clk(CLK), .Q(R6));  // open: clr
  Register #(.trigger("falling"), .width(32)) u_R7 (.D(WD3), .en(and_8_out), .clk(CLK), .Q(R7));  // open: clr
  Register #(.trigger("falling"), .width(32)) u_R8 (.D(WD3), .en(and_9_out), .clk(CLK), .Q(R8));  // open: clr
  Register #(.trigger("falling"), .width(32)) u_R9 (.D(WD3), .en(and_10_out), .clk(CLK), .Q(R9));  // open: clr
  Register #(.trigger("falling"), .width(32)) u_R10 (.D(WD3), .en(and_11_out), .clk(CLK), .Q(R10));  // open: clr
  and and_11 (and_11_out, Dec10, WE3);
  Register #(.trigger("falling"), .width(32)) u_R11 (.D(WD3), .en(and_12_out), .clk(CLK), .Q(R11));  // open: clr
  and and_12 (and_12_out, Dec11, WE3);
  Register #(.trigger("falling"), .width(32)) u_R12 (.D(WD3), .en(and_13_out), .clk(CLK), .Q(R12));  // open: clr
  and and_13 (and_13_out, Dec12, WE3);
  Register #(.trigger("falling"), .width(32)) u_R13 (.D(WD3), .en(and_14_out), .clk(CLK), .Q(R13));  // open: clr
  and and_14 (and_14_out, Dec13, WE3);
  Register #(.trigger("falling"), .width(32)) u_R14 (.D(WD3), .en(and_15_out), .clk(CLK), .Q(R14));  // open: clr
  and and_15 (and_15_out, Dec14, WE3);
  Multiplexer #(.select(4), .width(32)) multiplexer_1 (
    .in0(R0), .in1(R1), .in2(R2), .in3(R3), .in4(R4), .in5(R5), .in6(R6), .in7(R7), .in8(R8), .in9(R9),
    .in10(R10), .in11(R11), .in12(R12), .in13(R13), .in14(R14), .in15(R15), .out(RD1), .sel(A1));
  Multiplexer #(.select(4), .width(32)) multiplexer_2 (
    .in0(R0), .in1(R1), .in2(R2), .in3(R3), .in4(R4), .in5(R5), .in6(R6), .in7(R7), .in8(R8), .in9(R9),
    .in10(R10), .in11(R11), .in12(R12), .in13(R13), .in14(R14), .in15(R15), .out(RD2), .sel(A2));
endmodule

module Test (
  input  EN,
  input  RST,
  output [31:0] RD1_OUT,
  output [31:0] RD2_OUT
);

  wire CLK_out, registerfile_tb_1_we3;
  wire [3:0] registerfile_tb_1_a1, registerfile_tb_1_a2, registerfile_tb_1_a3;
  wire [31:0] registerfile_tb_1_r15, registerfile_tb_1_wd3;

  // Probe on registerfile_tb_1_a1
  // Probe on registerfile_tb_1_we3
  RegisterFile_TB registerfile_tb_1 (
    .CLK(registerfile_tb_1_we3), .RST(RST), .WE3(registerfile_tb_1_we3), .A1(registerfile_tb_1_a1),
    .A2(registerfile_tb_1_a2), .A3(registerfile_tb_1_a3), .WD3(registerfile_tb_1_wd3),
    .R15(registerfile_tb_1_r15));
  // Probe on registerfile_tb_1_a2
  Clock CLK (.out(CLK_out));
  and and_1 (registerfile_tb_1_we3, CLK_out, EN);
  // Probe on registerfile_tb_1_a3
  // Probe on registerfile_tb_1_wd3
  // Probe on registerfile_tb_1_r15
  RegisterFile registerfile_1 (
    .A1(registerfile_tb_1_a1), .A2(registerfile_tb_1_a2), .CLK(registerfile_tb_1_we3),
    .WE3(registerfile_tb_1_we3), .WD3(registerfile_tb_1_wd3), .A3(registerfile_tb_1_a3),
    .R15(registerfile_tb_1_r15), .RD1(RD1_OUT), .RD2(RD2_OUT));
endmodule

// VHDL entity RegisterFile_TB, as the project stores it:
library ieee; 
use ieee.std_logic_1164.all;
use ieee.numeric_std.all;

entity RegisterFile_TB is
	port(CLK	: in std_logic;
		RST	: in std_logic;
		WE3	: out std_logic;
		A1	: out std_logic_vector(3 downto 0);
		A2	: out std_logic_vector(3 downto 0);
		A3	: out std_logic_vector(3 downto 0);
		WD3	: out std_logic_vector(31 downto 0);
		R15	: out std_logic_vector(31 downto 0));
end;

architecture sim of RegisterFile_TB is
begin
	process(clk) is
		variable ticks : integer := 0;
		variable value : integer := 0;
		variable test_phase : std_logic := '0'; --0 for write phase, 1 for read phase
	begin
		if RST = '1' then
			ticks := 0;
			value := 0;
			test_phase:= '0'; --0 for write phase, 1 for read phase
		end if;
		if rising_edge(clk) then
			case test_phase is
				when '0' => --First start the verification by writing a unique value into each of the registers of the file
					WE3 <= '1';
					A3 <= std_logic_vector(to_unsigned(value, A3'length));
					WD3 <= std_logic_vector(to_unsigned(value, WD3'length));
					R15 <= std_logic_vector(to_unsigned(15, R15'length)); --TODO:Determine a better way to set this value as it shouldn't change
					value := value + 1;
				when '1' => --Read back out the values to ensure that the write operation was successful
					WE3 <= '0';
					A1 <= std_logic_vector(to_unsigned(value, a1'length));
					A2 <= std_logic_vector(to_unsigned(value + 1, a2'length));
					R15 <= std_logic_vector(to_unsigned(15, R15'length)); --TODO:Determine a better way to set this value as it shouldn't change
					value := value + 1;
				when others => --seems a bit unncessary to do this as I would assume that a std_logic type only has two possibles states
					WE3 <= '0';
					A1 <= "0000";
					A2 <= "0000";
					A3 <= "0000";
					WD3 <= std_logic_vector(to_unsigned(15, WD3'length));
					R15 <= std_logic_vector(to_unsigned(0, R15'length));
			end case;
			
			ticks := ticks + 1;

			if ticks = 15 then --Switch over to the read phase after all the values have been written
				test_phase := '1';
				value := 0;
			elsif ticks = 31 then --Set this be inactive and not change things after the tests have completed
				test_phase := 'Z';
			end if;
		end if;
	end process;
end architecture;
