// Logisim project ARM_Extend.circ as structural Verilog: 1 circuit, main circuit ARM_Extend
module ARM_Extend (
  input  [1:0] ImmSrc,
  input  [23:0] InstrImm,
  output [31:0] ExtImm
);

  Multiplexer #(.select(2), .width(32)) multiplexer_1 (
    .in0({{24{1'b0}}, InstrImm[7:0]}), .in1({{20{1'b0}}, InstrImm[11:0]}),
    .in2({{7{InstrImm[23]}}, InstrImm[22:0], 2'b00}), .out(ExtImm), .sel(ImmSrc));  // open: in3

  // Notes on the sheet:
  //   Replicate the sign-bit for the extension
  //   Dropped bits
  //   Perform arithmetic left-shift by 2 bits to acheive mutliplication by 4
  //   ImmSrc = 00 corresponds to extension of an unsigned 8-bit immediate for data processing instructions.
  //   ImmSrc = 01 corresponds to extension of an unsigned 12-bit immediate for memory instructions.
  //   ImmSrc = 10 corresponds to extension of an signed 24-bit immediate for branch instructions.
endmodule
